// Logisim project cpu3.circ as structural Verilog: 6 circuits, main circuit main
module main (
);

  wire alu_1_carry, alu_1_zero, and_1_out, and_2_out, and_3_out, and_4_out, and_5_out, and_6_out, and_7_out,
       and_8_out, and_9_out, and_10_out, buffer_1_out, buffer_3_out, buffer_4_out, buffer_5_out,
       buffer_6_out, buffer_7_out, buffer_8_out, buffer_9_out, buffer_10_out, buffer_11_out, buffer_12_out,
       buffer_13_out, buffer_14_out, buffer_15_out, buffer_16_out, clock_1_out, controlled_buffer_2_out,
       controlled_buffer_6_out, controlled_buffer_14_out, controlled_buffer_17_out, controlled_buffer_20_out,
       controlled_buffer_21_out, controlled_buffer_22_out, d_ff_1_q, d_ff_2_q, demultiplexer_1_out0,
       demultiplexer_1_out1, demultiplexer_1_out2, demultiplexer_1_out3, demultiplexer_2_out3,
       demultiplexer_2_out4, demultiplexer_2_out9, demultiplexer_2_out10, demultiplexer_2_out11,
       demultiplexer_4_out0, demultiplexer_4_out1, demultiplexer_4_out2, demultiplexer_4_out3,
       fallingedge_1_out_2, or_2_out, or_3_out, or_4_out, pull_resistor_1_node, pull_resistor_2_node,
       rgbled_1_p1, undriven_5;
  wire [1:0] buffer_2_out, counter_1_q, pla_1_out, undriven_4;
  wire [3:0] demultiplexer_2_out8;
  wire [7:0] alu_1_sum, controlled_buffer_1_out, controlled_buffer_3_out, controlled_buffer_4_out,
       controlled_buffer_5_out, controlled_buffer_15_out, controlled_buffer_16_out, counter_2_q,
       mmu_1_out_10, multiplexer_1_out, multiplexer_2_out, pull_resistor_7_node, pull_resistor_8_node,
       pull_resistor_9_node, register_1_q, register_2_q, register_3_q, register_4_q, register_5_q,
       rom_1_data, undriven, undriven_2, undriven_3;
  wire [14:0] mmu_1_romaddr;

  Demultiplexer #(.select(2)) demultiplexer_1 (
    .out0(demultiplexer_1_out0), .out1(demultiplexer_1_out1), .out2(demultiplexer_1_out2),
    .out3(demultiplexer_1_out3), .in(clock_1_out), .sel(counter_1_q));
  Counter #(.max('h2), .trigger("falling"), .width(2)) counter_1 (
    .Q(counter_1_q), .clk(buffer_1_out));  // open: load, D, count, carry, up, clr
  buf buffer_1 (buffer_1_out, clock_1_out);
  Clock clock_1 (.out(clock_1_out));
  // RGBLED rgbled_1: pin names not known; wires that end beside it: rgbled_1_p1, demultiplexer_1_out0
  or or_1 (rgbled_1_p1, demultiplexer_1_out1, demultiplexer_1_out2);
  // NoConnect on demultiplexer_1_out3
  FallingEdge fallingedge_1 (.out_2(fallingedge_1_out_2), .in_1(pull_resistor_1_node));
  Pull_Resistor pull_resistor_1 (.node(pull_resistor_1_node));
  assign controlled_buffer_1_out = demultiplexer_1_out0 ? counter_2_q : 8'bz;  // Controlled_Buffer controlled_buffer_1
  Counter #(.trigger("falling")) counter_2 (
    .load(pull_resistor_1_node), .D(undriven), .Q(counter_2_q), .clk(or_2_out));  // open: count, carry, up, clr
  or or_2 (or_2_out, demultiplexer_1_out0, or_3_out);
  or or_3 (or_3_out, fallingedge_1_out_2, pull_resistor_2_node);
  Pull_Resistor pull_resistor_2 (.node(pull_resistor_2_node));
  Register #(.trigger("falling")) register_1 (
    .D(mmu_1_out_10), .Q(register_1_q), .clk(demultiplexer_1_out0));  // open: en, clr
  assign controlled_buffer_2_out = demultiplexer_1_out0 ? demultiplexer_1_out0 : 1'bz;  // Controlled_Buffer controlled_buffer_2
  assign buffer_2_out = register_1_q[6:5];  // Buffer buffer_2, 2 bits wide
  assign controlled_buffer_3_out = demultiplexer_2_out3 ? multiplexer_2_out : 8'bz;  // Controlled_Buffer controlled_buffer_3
  assign controlled_buffer_4_out = demultiplexer_2_out4 ? multiplexer_2_out : 8'bz;  // Controlled_Buffer controlled_buffer_4
  and and_1 (and_1_out, demultiplexer_1_out1, demultiplexer_2_out3);
  and and_2 (and_2_out, demultiplexer_1_out1, demultiplexer_2_out4);
  PLA #(.in_width(4), .\table ("1000 00 # 0\n0100 01 # 1\n0010 10 # 2\n0001 11 # 3")) pla_1 (
    .in(demultiplexer_2_out8), .out(pla_1_out));
  Multiplexer #(.select(2), .width(8)) multiplexer_1 (
    .in0(register_2_q), .in1(register_3_q), .in2(register_4_q), .in3(register_5_q), .out(multiplexer_1_out),
    .sel(pla_1_out));
  assign controlled_buffer_5_out = and_3_out ? multiplexer_1_out : 8'bz;  // Controlled_Buffer controlled_buffer_5
  buf buffer_3 (buffer_3_out, and_3_out);
  buf buffer_4 (buffer_4_out, buffer_3_out);
  assign controlled_buffer_6_out = and_3_out ? buffer_4_out : 1'bz;  // Controlled_Buffer controlled_buffer_6
  and and_3 (and_3_out, demultiplexer_1_out1, or_4_out);
  or or_4 (or_4_out, demultiplexer_2_out8[3], demultiplexer_2_out8[2], demultiplexer_2_out8[1], demultiplexer_2_out8[0]);
  buf buffer_5 (buffer_5_out, and_7_out);
  buf buffer_6 (buffer_6_out, buffer_5_out);
  buf buffer_7 (buffer_7_out, buffer_6_out);
  buf buffer_8 (buffer_8_out, buffer_7_out);
  assign controlled_buffer_2_out = and_7_out ? buffer_8_out : 1'bz;  // Controlled_Buffer controlled_buffer_7
  assign controlled_buffer_1_out = and_7_out ? counter_2_q : 8'bz;  // Controlled_Buffer controlled_buffer_8
  assign controlled_buffer_5_out = and_5_out ? mmu_1_out_10 : 8'bz;  // Controlled_Buffer controlled_buffer_9
  buf buffer_9 (buffer_9_out, and_5_out);
  buf buffer_10 (buffer_10_out, buffer_9_out);
  assign controlled_buffer_6_out = and_5_out ? buffer_10_out : 1'bz;  // Controlled_Buffer controlled_buffer_10
  and and_4 (and_4_out, rgbled_1_p1, ~register_1_q[7]);  // AND_Gate
  Demultiplexer #(.select(5)) demultiplexer_2 (
    .out3(demultiplexer_2_out3), .out4(demultiplexer_2_out4), .out5(demultiplexer_2_out8[3]),
    .out6(demultiplexer_2_out8[2]), .out7(demultiplexer_2_out8[1]), .out8(demultiplexer_2_out8[0]),
    .out9(demultiplexer_2_out9), .out10(demultiplexer_2_out10), .out11(demultiplexer_2_out11),
    .in(and_4_out), .sel(register_1_q[4:0]));  // open: out0, out1, out2, out12, out13, out14, out15, out16, out17, out18, out19, out20, out21, out22, out23, out24, out25, out26, out27, out28, out29, out30, out31
  assign pull_resistor_2_node = and_5_out ? and_5_out : 1'bz;  // Controlled_Buffer controlled_buffer_11
  and and_5 (and_5_out, demultiplexer_2_out9, demultiplexer_1_out2);
  and and_6 (and_6_out, demultiplexer_1_out1, demultiplexer_2_out10);
  and and_7 (and_7_out, demultiplexer_2_out9, demultiplexer_1_out1);
  assign controlled_buffer_1_out = and_6_out ? multiplexer_2_out : 8'bz;  // Controlled_Buffer controlled_buffer_12
  and and_8 (and_8_out, demultiplexer_2_out10, demultiplexer_1_out2);
  and and_9 (and_9_out, demultiplexer_1_out1, demultiplexer_2_out11);
  buf buffer_11 (buffer_11_out, and_6_out);
  buf buffer_12 (buffer_12_out, and_8_out);
  buf buffer_13 (buffer_13_out, buffer_11_out);
  buf buffer_14 (buffer_14_out, buffer_12_out);
  assign controlled_buffer_2_out = and_6_out ? buffer_13_out : 1'bz;  // Controlled_Buffer controlled_buffer_13
  assign controlled_buffer_14_out = and_8_out ? buffer_14_out : 1'bz;  // Controlled_Buffer controlled_buffer_14
  assign controlled_buffer_15_out = and_8_out ? mmu_1_out_10 : 8'bz;  // Controlled_Buffer controlled_buffer_15
  buf buffer_15 (buffer_15_out, and_9_out);
  assign controlled_buffer_16_out = and_9_out ? register_2_q : 8'bz;  // Controlled_Buffer controlled_buffer_16
  buf buffer_16 (buffer_16_out, buffer_15_out);
  assign controlled_buffer_17_out = and_9_out ? buffer_16_out : 1'bz;  // Controlled_Buffer controlled_buffer_17
  assign controlled_buffer_1_out = and_9_out ? multiplexer_2_out : 8'bz;  // Controlled_Buffer controlled_buffer_18
  and and_10 (and_10_out, rgbled_1_p1, register_1_q[7]);
  Demultiplexer #(.select(5)) demultiplexer_3 (
    .in(and_10_out), .sel(register_1_q[4:0]));  // open: out0, out1, out2, out3, out4, out5, out6, out7, out8, out9, out10, out11, out12, out13, out14, out15, out16, out17, out18, out19, out20, out21, out22, out23, out24, out25, out26, out27, out28, out29, out30, out31
  ROM #(.addrWidth(15)) rom_1 (.addr(mmu_1_romaddr), .data(rom_1_data));
  Pull_Resistor pull_resistor_3 (.node(controlled_buffer_2_out));
  Pull_Resistor pull_resistor_4 (.node(controlled_buffer_17_out));
  Pull_Resistor pull_resistor_5 (.node(controlled_buffer_6_out));
  assign controlled_buffer_14_out = demultiplexer_4_out0 ? demultiplexer_4_out0 : 1'bz;  // Controlled_Buffer controlled_buffer_19
  Demultiplexer #(.select(2)) demultiplexer_4 (
    .out0(demultiplexer_4_out0), .out1(demultiplexer_4_out1), .out2(demultiplexer_4_out2),
    .out3(demultiplexer_4_out3), .in(controlled_buffer_6_out), .sel(buffer_2_out));
  assign controlled_buffer_20_out = demultiplexer_4_out3 ? demultiplexer_4_out3 : 1'bz;  // Controlled_Buffer controlled_buffer_20
  D_Flip_Flop d_ff_1 (.D(alu_1_zero), .clk(undriven_5), .Q(d_ff_1_q));  // open: Qn, preset, reset
  D_Flip_Flop d_ff_2 (.D(alu_1_carry), .clk(undriven_5), .Q(d_ff_2_q));  // open: Qn, preset, reset
  MMU mmu_1 (
    .out_10(mmu_1_out_10), .ROMADDR(mmu_1_romaddr), .RAMBNK(controlled_buffer_3_out), .RAMBNKSET(and_1_out),
    .ROMBNK(controlled_buffer_4_out), .ROMBNKSET(and_2_out), .ADDR(controlled_buffer_1_out),
    .RD(controlled_buffer_2_out), .WRT(controlled_buffer_17_out), .VAL(controlled_buffer_16_out),
    .ROMOUT(rom_1_data));
  assign controlled_buffer_21_out = demultiplexer_4_out1 ? demultiplexer_4_out1 : 1'bz;  // Controlled_Buffer controlled_buffer_21
  assign controlled_buffer_22_out = demultiplexer_4_out2 ? demultiplexer_4_out2 : 1'bz;  // Controlled_Buffer controlled_buffer_22
  ALU alu_1 (.Carry(alu_1_carry), .Sum(alu_1_sum), .Zero(alu_1_zero), .Sel(undriven_4), .A(undriven_2), .B(undriven_3));
  Pull_Resistor pull_resistor_6 (.node(controlled_buffer_15_out));
  assign controlled_buffer_15_out = controlled_buffer_6_out ? controlled_buffer_5_out : 8'bz;  // Controlled_Buffer controlled_buffer_23
  Pull_Resistor pull_resistor_7 (.node(pull_resistor_7_node));
  assign pull_resistor_7_node = controlled_buffer_6_out ? controlled_buffer_5_out : 8'bz;  // Controlled_Buffer controlled_buffer_24
  Pull_Resistor pull_resistor_8 (.node(pull_resistor_8_node));
  assign pull_resistor_8_node = controlled_buffer_6_out ? controlled_buffer_5_out : 8'bz;  // Controlled_Buffer controlled_buffer_25
  Pull_Resistor pull_resistor_9 (.node(pull_resistor_9_node));
  assign pull_resistor_9_node = controlled_buffer_6_out ? controlled_buffer_5_out : 8'bz;  // Controlled_Buffer controlled_buffer_26
  Pull_Resistor pull_resistor_10 (.node(controlled_buffer_14_out));
  Pull_Resistor pull_resistor_11 (.node(controlled_buffer_21_out));
  Pull_Resistor pull_resistor_12 (.node(controlled_buffer_22_out));
  Pull_Resistor pull_resistor_13 (.node(controlled_buffer_20_out));
  Register register_2 (
    .D(controlled_buffer_15_out), .Q(register_2_q), .clk(controlled_buffer_14_out));  // open: en, clr
  Register register_3 (.D(pull_resistor_7_node), .Q(register_3_q), .clk(controlled_buffer_21_out));  // open: en, clr
  Register register_4 (.D(pull_resistor_8_node), .Q(register_4_q), .clk(controlled_buffer_22_out));  // open: en, clr
  Register register_5 (.D(pull_resistor_9_node), .Q(register_5_q), .clk(controlled_buffer_20_out));  // open: en, clr
  Multiplexer #(.select(2), .width(8)) multiplexer_2 (
    .in0(register_2_q), .in1(register_3_q), .in2(register_4_q), .in3(register_5_q), .out(multiplexer_2_out),
    .sel(buffer_2_out));

  // Notes on the sheet:
  //   BNKROMV
  //   BNKRAMWRT
  //   BNKROMWRT
  //   PC
  //   BNKRAMV
  //   ADDR
  //   WRTVAL
  //   RD
  //   WR
  //   OUT
  //   WR_SEL_V
  //   WR_SEL
  //   SEL
  //   SEL_VAL
  //   A_VAL
  //   B_VAL
  //   C_VAL
  //   D_VAL
  //   WR_A_VAL
  //   WR_B_VAL
  //   WR_C_VAL
  //   WR_D_VAL
  //   WR_A
  //   WR_B
  //   WR_C
  //   WR_D
  //   ALU_A
  //   ALU_B
  //   ALU_Z
  //   ALU_C
  //   ALU_R
  //   ALU_S
  //   C_FLAG
  //   Z_FLAG
  //   FLAG
  //   skip pc
  //   t1/t2
  //   BANK
  //   LD R,R
  //   LD R,V
  //   LD A,[R]
  //   LD [R],A
  //   JUMP
  //   JADDR
  //   PC
  //   contents of rom_1 (hex, n*v repeats v):
  //   9 69 49 81 69 ff 0 0 4b 6b 6*0 9 0 29 5*0 6a 25 4a
endmodule

module MMU (
  input  [7:0] ROMOUT,
  input  [7:0] RAMBNK,
  input  [7:0] ROMBNK,
  input  [7:0] ADDR,
  input  [7:0] VAL,
  input  RAMBNKSET,
  input  ROMBNKSET,
  input  RD,
  input  WRT,
  output [7:0] out_10,
  output [14:0] ROMADDR
);

  wire and_1_out, and_2_out, and_3_out, buffer_2_out, buffer_4_out, buffer_6_out, buffer_8_out, not_1_out,
       or_3_out;
  wire [7:0] buffer_1_out, buffer_3_out, buffer_5_out, buffer_7_out, errorpulldown8_1_out_2,
       multiplexer_1_out, ram_1_dout, register_1_q, register_2_q;
  wire [14:0] bit_extender_1_out, bit_extender_2_out, bit_extender_3_out, or_1_out, or_2_out, shifter_1_out,
       shifter_2_out;

  assign buffer_1_out = RAMBNK;  // Buffer buffer_1, 8 bits wide
  buf buffer_2 (buffer_2_out, RAMBNKSET);
  Pull_Resistor pull_resistor_1 (.node(RAMBNK));
  Pull_Resistor pull_resistor_2 (.node(RAMBNKSET));
  assign buffer_3_out = ROMBNK;  // Buffer buffer_3, 8 bits wide
  buf buffer_4 (buffer_4_out, ROMBNKSET);
  assign buffer_5_out = ADDR;  // Buffer buffer_5, 8 bits wide
  Pull_Resistor pull_resistor_3 (.node(ROMBNK));
  Pull_Resistor pull_resistor_4 (.node(ROMBNKSET));
  Pull_Resistor pull_resistor_5 (.node(ADDR));
  assign bit_extender_1_out = {{7{1'b0}}, register_1_q};  // Bit_Extender bit_extender_1
  Register register_1 (.D(buffer_1_out), .Q(register_1_q), .clk(buffer_2_out));  // open: en, clr
  assign bit_extender_2_out = {{8{1'b0}}, buffer_5_out[6:0]};  // Bit_Extender bit_extender_2
  assign bit_extender_3_out = {{7{1'b0}}, register_2_q};  // Bit_Extender bit_extender_3
  Register register_2 (.D(buffer_3_out), .Q(register_2_q), .clk(buffer_4_out));  // open: en, clr
  Shifter #(.width(15)) shifter_1 (.in(bit_extender_1_out), .\dist (4'b0111), .out(shifter_1_out));
  Shifter #(.width(15)) shifter_2 (.in(bit_extender_3_out), .\dist (4'b0111), .out(shifter_2_out));
  assign or_1_out = shifter_1_out | bit_extender_2_out;  // OR_Gate or_1, 15 bits wide
  assign or_2_out = bit_extender_2_out | shifter_2_out;  // OR_Gate or_2, 15 bits wide
  Register #(.trigger("high"), .width(15)) register_3 (.D(or_2_out), .Q(ROMADDR), .clk(and_3_out));  // open: en, clr
  and and_1 (and_1_out, buffer_5_out[7], or_3_out);
  and and_2 (and_2_out, buffer_5_out[7], buffer_8_out);
  or or_3 (or_3_out, buffer_6_out, buffer_8_out);
  buf buffer_6 (buffer_6_out, RD);
  Pull_Resistor pull_resistor_6 (.node(RD));
  RAM #(.addrWidth(15)) ram_1 (
    .addr(or_1_out), .we(and_2_out), .oe(and_1_out), .clk(and_1_out), .din(buffer_7_out), .dout(ram_1_dout));
  assign buffer_7_out = VAL;  // Buffer buffer_7, 8 bits wide
  Pull_Resistor pull_resistor_7 (.node(VAL));
  buf buffer_8 (buffer_8_out, WRT);
  Pull_Resistor pull_resistor_8 (.node(WRT));
  and and_3 (and_3_out, ~buffer_5_out[7], or_3_out);  // AND_Gate
  ErrorPullDown8 errorpulldown8_1 (.out_2({errorpulldown8_1_out_2[7], ram_1_dout[7], errorpulldown8_1_out_2[6], ram_1_dout[6], errorpulldown8_1_out_2[5], ram_1_dout[5], errorpulldown8_1_out_2[4], ram_1_dout[4], errorpulldown8_1_out_2[3], ram_1_dout[3], errorpulldown8_1_out_2[2], ram_1_dout[2], errorpulldown8_1_out_2[1], ram_1_dout[1], errorpulldown8_1_out_2[0], ram_1_dout[0]}));
  Multiplexer #(.width(8)) multiplexer_1 (
    .in0(errorpulldown8_1_out_2), .in1(ROMOUT), .out(multiplexer_1_out), .sel(not_1_out));
  not not_1 (not_1_out, buffer_5_out[7]);
  Register #(.trigger("high")) register_4 (.D(multiplexer_1_out), .Q(out_10), .clk(or_3_out));  // open: en, clr
endmodule

module MMUtest (
);

  wire button_1_out, button_2_out, button_3_out, button_4_out;
  wire [7:0] mmu_1_out_10, rom_1_data, undriven, undriven_2, undriven_3, undriven_4;
  wire [14:0] mmu_1_romaddr;

  // DipSwitch dipswitch_1: pin names not known
  Button button_1 (.out(button_1_out));
  // DipSwitch dipswitch_2: pin names not known
  // DipSwitch dipswitch_3: pin names not known
  Button button_2 (.out(button_2_out));
  // DipSwitch dipswitch_4: pin names not known
  Button button_3 (.out(button_3_out));
  Button button_4 (.out(button_4_out));
  ROM #(.addrWidth(15)) rom_1 (.addr(mmu_1_romaddr), .data(rom_1_data));
  DotMatrix #(.inputtype("row"), .matrixcols(8), .matrixrows(1)) dotmatrix_1 (.row0(mmu_1_out_10));
  MMU mmu_1 (
    .out_10(mmu_1_out_10), .ROMADDR(mmu_1_romaddr), .RAMBNK(undriven), .RAMBNKSET(button_1_out),
    .ROMBNK(undriven_2), .ROMBNKSET(button_2_out), .ADDR(undriven_3), .RD(button_3_out), .WRT(button_4_out),
    .VAL(undriven_4), .ROMOUT(rom_1_data));
endmodule

module ErrorPullDown8 (
  input  [7:0] in_1,
  output [7:0] out_2
);


  assign out_2 = in_1;

  // Notes on the sheet:
  //   in_1: pull=down
  //   out_2: pull=down
endmodule

module FallingEdge (
  input  in_1,
  output out_2
);

  wire not_1_out, not_2_out, not_3_out;

  not not_1 (not_1_out, in_1);
  not not_2 (not_2_out, not_1_out);
  not not_3 (not_3_out, not_2_out);
  and and_1 (out_2, in_1, not_3_out);
endmodule

module ALU (
  input  [7:0] A,
  input  [7:0] B,
  input  [1:0] Sel,
  output Carry,
  output [7:0] Sum,
  output Zero
);

  wire [2:0] comparator_1_eq;
  wire [7:0] adder_1_out, bit_extender_1_out, multiplier_1_out, subtractor_1_out;

  Adder adder_1 (.a(A), .b(B), .out(adder_1_out), .cout(Carry));  // open: cin
  Subtractor subtractor_1 (.a(A), .b(B), .out(subtractor_1_out), .bout(Carry));  // open: bin
  Comparator #(.mode("unsigned")) comparator_1 (
    .a(A), .b(B), .gt(comparator_1_eq[1]), .eq(comparator_1_eq[0]), .lt(comparator_1_eq[2]));
  Multiplier multiplier_1 (.a(A), .b(B), .out(multiplier_1_out));  // open: cin, cout
  assign bit_extender_1_out = {{5{1'b0}}, comparator_1_eq};  // Bit_Extender bit_extender_1
  Multiplexer #(.select(2), .width(8)) multiplexer_1 (
    .in0(adder_1_out), .in1(subtractor_1_out), .in2(bit_extender_1_out), .in3(multiplier_1_out), .out(Sum),
    .sel(Sel));
  Comparator #(.mode("unsigned")) comparator_2 (.a(Sum), .b({8{1'b0}}), .eq(Zero));  // open: gt, lt
endmodule
